# Fritzing sketch Breadboard_Design_v3 (saved by Fritzing 0.9.4)
circuit board: 13.141cm x 6.58314cm
breadboards: 1

parts:
  REG1 = Voltage Regulator [part_number=296-39515-5-ND package=to-220-alt]
  C2 = Capacitor Polarized [part_number=1189-2322-ND package=panasonic_e]
  IC1 = IC, DIP package, 28 pins [chip_label=IC part_number=ATMEGA328P-PN-ND]
  PWR = LED - 5mm [color="Red (633nm)" package="5 mm [THT]"]
  R1 = Resistor [tolerance=±5% resistance=330 part_number=CF14JT330RCT-ND package=THT]
  XTAL1 = Crystal [frequency="16 Mhz" part_number=XC1925-ND package=THT]
  C3 = Ceramic Capacitor [capacitance=22pF part_number=BC1005CT-ND voltage=50V package="100 mil [THT, multilayer]"]
  C4 = Ceramic Capacitor [capacitance=22pF part_number=BC1005CT-ND voltage=50V package="100 mil [THT, multilayer]"]
  RESET = Pushbutton [part_number=679-2428-ND package="[THT]"]
  R2 = Resistor [tolerance=±5% resistance=10k part_number=CFR-25JB-52-10K package=THT]
  ACT = LED - 5mm [color="Yellow (585nm)" package="5 mm [THT]"]
  R3 = Resistor [tolerance=±5% resistance=330 part_number=CF14JT330RCT-ND package=THT]
  MAX4466 = Adafruit MAX4466 Electret Microphone Amplifier [part_number="Adafruit #1063"]
  CON1 = Adafruit I2C+SPI LCD Backpack [part_number="Adafruit #292"]
  STOR1 = I2C Non-Volatile FRAM 32KB [part_number="Adafruit #1895"]
  U1 = LCD-16X2 [package=lcd-16x2]
  Contrast = POT [package=trim_pot]
  C1 = Capacitor Polarized [part_number=1189-2322-ND package=panasonic_e]
  UP = Pushbutton [part_number=679-2428-ND package="[THT]"]  # not connected
  DOWN = Pushbutton [part_number=679-2428-ND package="[THT]"]  # not connected
  RIGHT = Pushbutton [part_number=679-2428-ND package="[THT]"]  # not connected
  ENTER = Pushbutton [part_number=679-2428-ND package="[THT]"]  # not connected
  LEFT = Pushbutton [part_number=679-2428-ND package="[THT]"]  # not connected

nets:
  GND: REG1.GND, C2.-, IC1.pin8, IC1.pin22, R1.Pin_1, C3.1, C4.1, RESET.Pin_1, RESET.Pin_2, R3.Pin_1, MAX4466.GND, CON1.GND, STOR1.GND, U1.VSS, U1.R_W, Contrast.E, C1.-
  N1: REG1.IN, C1.+
  N2: REG1.OUT, C2.+, PWR.anode
  N3: IC1.pin1, RESET.Pin_3, RESET.Pin_4, R2.Pin_1
  VCC: IC1.pin7, IC1.pin20, IC1.pin21, PWR.cathode, R1.Pin_0, R2.Pin_0, MAX4466.VCC, CON1.VCC, STOR1.VCC, U1.VDD, U1.A, Contrast.A
  N4: IC1.pin9, XTAL1.pin_0, C3.0
  N5: IC1.pin10, XTAL1.pin_1, C4.0
  N6: IC1.pin23, ACT.anode
  N7: IC1.pin24, MAX4466.OUT
  N8: IC1.pin27, CON1.DATA, STOR1.SDA
  N9: IC1.pin28, CON1.CLOCK, STOR1.SCL
  N10: ACT.cathode, R3.Pin_0
  N11: CON1.CONTRAST, U1.VO, Contrast.S
  N12: CON1.RS, U1.RS
  N13: CON1.E, U1.E
  N14: CON1.DB0, U1.DB0
  N15: CON1.DB1, U1.DB1
  N16: CON1.DB2, U1.DB2
  N17: CON1.DB3, U1.DB3
  N18: CON1.DB4, U1.DB4
  N19: CON1.DB5, U1.DB5
  N20: CON1.DB6, U1.DB6
  N21: CON1.DB7, U1.DB7
  N22: CON1.LEDK, U1.K

custom parts:
  Adafruit MAX4466 Electret Microphone Amplifier: Add an ear to your project with this well-designed electret microphone amplifier. This fully assembled and tested board comes with a 20-20KHz electret microphone soldered on. For the amplification, we use the Maxim MAX4466, an op-amp specifically designed for this delicate task! The amplifier has excellent power supply noise rejection, so this amplifier sounds really good and isn't nearly as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
  Adafruit I2C+SPI LCD Backpack: LCD backpacks reduce the number of pins needed to connect to an LCD. LCDs are a fun and easy way to have your microcontroller project talk back to you. Character LCDs are common, and easy to get, available in tons of colors and sizes. We've written tutorials on using character LCDs with an Arduino (or similar microcontroller) but find that the number of pins necessary to control the LCD can be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
  I2C Non-Volatile FRAM 32KB: With our I2C FRAM breakout board you can add some FRAM storage to your next DIY project. FRAM allows for a lower power usage and a faster write performance. It's excellent for low-power or inconsistent-power datalogging or data buffering where you want to stream data fast while also keeping the data when there's no power. Unlike Flash or EEPROM there's no pages to worry about. Each byte can be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
